// Logisim project alu_harness.circ as structural Verilog: 2 circuits, main circuit main
module main (
  output [7:0] Test,
  output [31:0] Result,
  output [3:0] ALU_Sel,
  output [31:0] Input_A,
  output [31:0] Input_B
);

  wire clock_1_out;
  wire [7:0] adder_1_out;

  Clock clock_1 (.out(clock_1_out));
  Adder adder_1 (.a(8'h1), .b(Test), .out(adder_1_out));  // open: cin, cout
  Register register_1 (.D(adder_1_out), .clk(clock_1_out), .Q(Test));  // open: en, clr
  ROM #(.dataWidth(32)) rom_1 (.addr(Test), .data(Input_A));
  // Probe on Input_B
  ROM #(.dataWidth(32)) rom_2 (.addr(Test), .data(Input_B));
  // Probe on Input_A
  // Probe on ALU_Sel
  ALUsadness alusadness_1 (.in_1(Input_A), .in_2(Input_B), .in_3(ALU_Sel), .out_4(Result));
  ROM #(.dataWidth(4)) rom_3 (.addr(Test), .data(ALU_Sel));

  // Notes on the sheet:
  //   Your ALU must fit here!
  //   There should be no red or blue wires, and the result should not be all X's
endmodule

module ALUsadness (
  input  [31:0] in_1,
  input  [31:0] in_2,
  input  [3:0] in_3,
  output [31:0] out_4
);

  wire [31:0] add0, and1, not4, or2, sll6, slt7, sra5, sub8, xor3;

  Adder #(.width(32)) adder_1 (.a(in_1), .b(in_2), .out(add0));  // open: cin, cout
  assign and1 = in_1 & in_2;  // AND_Gate and_1, 32 bits wide
  assign or2 = in_1 | in_2;  // OR_Gate or_1, 32 bits wide
  assign xor3 = in_1 ^ in_2;  // XOR_Gate xor_1, 32 bits wide
  assign not4 = ~in_1;  // NOT_Gate not_1, 32 bits wide
  Shifter #(.width(32), .shift("lr")) shifter_1 (.in(in_1), .\dist (in_2[4:0]), .out(sra5));
  Shifter #(.width(32)) shifter_2 (.in(in_1), .\dist (in_2[4:0]), .out(sll6));
  Subtractor #(.width(32)) subtractor_1 (.a(in_1), .b(in_2), .out(sub8));  // open: bin, bout
  assign slt7 = {{31{1'b0}}, sub8[31]};  // Bit_Extender bit_extender_1
  Multiplexer #(.select(4), .width(32), .enable("false")) multiplexer_1 (
    .in0(add0), .in1(and1), .in2(or2), .in3(xor3), .in4(not4), .in5(sra5), .in6(sll6), .in7(slt7),
    .in8(sub8), .out(out_4), .sel(in_3));  // open: in9, in10, in11, in12, in13, in14, in15

  // Other names for the same wires on the sheet: A[31:0] = in_1; ALUSel[3:0] = in_3; B[31:0] = in_2;
  //   result[31:0] = out_4

  // Notes on the sheet:
  //   INPUTS to your circuit
  //   OUTPUT from your circuit
endmodule
