// Logisim project branch_comp.circ as structural Verilog: 3 circuits, main circuit branch_comp
module branch_comp (
  input  [31:0] rs1,
  input  [31:0] rs2,
  input  BrUn,
  output BrEq,
  output BrLt
);

  wire compsigned_1_beq, compsigned_1_bless, compunsigned_1_beq, compunsigned_1_bless;

  compsigned compsigned_1 (.in_1(rs1), .in_2(rs2), .BLess(compsigned_1_bless), .BEq(compsigned_1_beq));
  compunsigned compunsigned_1 (.in_1(rs1), .in_2(rs2), .BLess(compunsigned_1_bless), .BEq(compunsigned_1_beq));
  Multiplexer #(.enable("false")) multiplexer_1 (
    .in0(compsigned_1_beq), .in1(compunsigned_1_beq), .out(BrEq), .sel(BrUn));
  Multiplexer #(.enable("false")) multiplexer_2 (
    .in0(compsigned_1_bless), .in1(compunsigned_1_bless), .out(BrLt), .sel(BrUn));

  // Notes on the sheet:
  //   INPUTS to your circuit
  //   DON'T CHANGE THE LOCATIONS OF THE INPUTS AND OUTPUTS!
  //   OUTPUT from your circuit
endmodule

module compunsigned (
  input  [31:0] in_1,
  input  [31:0] in_2,
  output BLess,
  output BEq
);

  wire C0, C1, C2, C3, C4, C5, C6, C7, C8, C9, C10, C11, C12, C13, C14, C15, C16, C17, C18, C19, C20, C21,
       C22, C23, C24, C25, C26, C27, C28, C29, C30, C31;
  wire [30:0] SUB;

  xnor xnor_1 (C0, in_1[0], in_2[0]);
  xnor xnor_2 (C1, in_1[1], in_2[1]);
  xnor xnor_3 (C2, in_1[2], in_2[2]);
  xnor xnor_4 (C3, in_1[3], in_2[3]);
  xnor xnor_5 (C4, in_1[4], in_2[4]);
  xnor xnor_6 (C5, in_1[5], in_2[5]);
  and and_1 (BEq, C0, C1, C2, C3, C4, C5, C6, C7, C8, C9, C10, C11, C12, C13, C14, C15, C16, C17, C18, C19, C20, C21, C22, C23, C24, C25, C26, C27, C28, C29, C30, C31);
  xnor xnor_7 (C16, in_1[16], in_2[16]);
  xnor xnor_8 (C17, in_1[17], in_2[17]);
  xnor xnor_9 (C6, in_1[6], in_2[6]);
  xnor xnor_10 (C7, in_1[7], in_2[7]);
  xnor xnor_11 (C18, in_1[18], in_2[18]);
  xnor xnor_12 (C19, in_1[19], in_2[19]);
  sub32 sub32_1 (.in_1(in_1), .in_2(in_2), .in_3(1'b1), .out_4({BLess, SUB}));  // open: Cout
  xnor xnor_13 (C8, in_1[8], in_2[8]);
  xnor xnor_14 (C9, in_1[9], in_2[9]);
  xnor xnor_15 (C20, in_1[20], in_2[20]);
  xnor xnor_16 (C21, in_1[21], in_2[21]);
  xnor xnor_17 (C10, in_1[10], in_2[10]);
  xnor xnor_18 (C11, in_1[11], in_2[11]);
  xnor xnor_19 (C22, in_1[22], in_2[22]);
  xnor xnor_20 (C23, in_1[23], in_2[23]);
  xnor xnor_21 (C12, in_1[12], in_2[12]);
  xnor xnor_22 (C13, in_1[13], in_2[13]);
  xnor xnor_23 (C24, in_1[24], in_2[24]);
  xnor xnor_24 (C25, in_1[25], in_2[25]);
  xnor xnor_25 (C14, in_1[14], in_2[14]);
  xnor xnor_26 (C15, in_1[15], in_2[15]);
  xnor xnor_27 (C26, in_1[26], in_2[26]);
  xnor xnor_28 (C27, in_1[27], in_2[27]);
  xnor xnor_29 (C28, in_1[28], in_2[28]);
  xnor xnor_30 (C29, in_1[29], in_2[29]);
  xnor xnor_31 (C30, in_1[30], in_2[30]);
  xnor xnor_32 (C31, in_1[31], in_2[31]);

  // Other names for the same wires on the sheet: A[31:0] = in_1; A0 = in_1[0]; A1 = in_1[1]; A2 = in_1[2];
  //   A3 = in_1[3]; A4 = in_1[4]; A5 = in_1[5]; A6 = in_1[6]; A7 = in_1[7]; A8 = in_1[8]; A9 = in_1[9];
  //   A10 = in_1[10]; A11 = in_1[11]; A12 = in_1[12]; A13 = in_1[13]; A14 = in_1[14]; A15 = in_1[15]; A16 = in_1[16];
  //   A17 = in_1[17]; A18 = in_1[18]; A19 = in_1[19]; A20 = in_1[20]; A21 = in_1[21]; A22 = in_1[22]; A23 = in_1[23];
  //   A24 = in_1[24]; A25 = in_1[25]; A26 = in_1[26]; A27 = in_1[27]; A28 = in_1[28]; A29 = in_1[29]; A30 = in_1[30];
  //   A31 = in_1[31]; B[31:0] = in_2; B0 = in_2[0]; B1 = in_2[1]; B2 = in_2[2]; B3 = in_2[3]; B4 = in_2[4];
  //   B5 = in_2[5]; B6 = in_2[6]; B7 = in_2[7]; B8 = in_2[8]; B9 = in_2[9]; B10 = in_2[10]; B11 = in_2[11];
  //   B12 = in_2[12]; B13 = in_2[13]; B14 = in_2[14]; B15 = in_2[15]; B16 = in_2[16]; B17 = in_2[17]; B18 = in_2[18];
  //   B19 = in_2[19]; B20 = in_2[20]; B21 = in_2[21]; B22 = in_2[22]; B23 = in_2[23]; B24 = in_2[24]; B25 = in_2[25];
  //   B26 = in_2[26]; B27 = in_2[27]; B28 = in_2[28]; B29 = in_2[29]; B30 = in_2[30]; B31 = in_2[31]; SUB[31] = BLess
endmodule

module compsigned (
  input  [31:0] in_1,
  input  [31:0] in_2,
  output BLess,
  output BEq
);

  wire C0, C1, C2, C3, C4, C5, C6, C7, C8, C9, C10, C11, C12, C13, C14, C15, C16, C17, C18, C19, C20, C21,
       C22, C23, C24, C25, C26, C27, C28, C29, C30, C31;

  xnor xnor_1 (C0, in_1[0], in_2[0]);
  xnor xnor_2 (C1, in_1[1], in_2[1]);
  xnor xnor_3 (C2, in_1[2], in_2[2]);
  xnor xnor_4 (C3, in_1[3], in_2[3]);
  xnor xnor_5 (C4, in_1[4], in_2[4]);
  xnor xnor_6 (C5, in_1[5], in_2[5]);
  and and_1 (BEq, C0, C1, C2, C3, C4, C5, C6, C7, C8, C9, C10, C11, C12, C13, C14, C15, C16, C17, C18, C19, C20, C21, C22, C23, C24, C25, C26, C27, C28, C29, C30, C31);
  xnor xnor_7 (C16, in_1[16], in_2[16]);
  xnor xnor_8 (C17, in_1[17], in_2[17]);
  xnor xnor_9 (C6, in_1[6], in_2[6]);
  xnor xnor_10 (C7, in_1[7], in_2[7]);
  xnor xnor_11 (C18, in_1[18], in_2[18]);
  xnor xnor_12 (C19, in_1[19], in_2[19]);
  slt slt_1 (.in_1(in_1), .in_2(in_2), .out_3(BLess));
  xnor xnor_13 (C8, in_1[8], in_2[8]);
  xnor xnor_14 (C9, in_1[9], in_2[9]);
  xnor xnor_15 (C20, in_1[20], in_2[20]);
  xnor xnor_16 (C21, in_1[21], in_2[21]);
  xnor xnor_17 (C10, in_1[10], in_2[10]);
  xnor xnor_18 (C11, in_1[11], in_2[11]);
  xnor xnor_19 (C22, in_1[22], in_2[22]);
  xnor xnor_20 (C23, in_1[23], in_2[23]);
  xnor xnor_21 (C12, in_1[12], in_2[12]);
  xnor xnor_22 (C13, in_1[13], in_2[13]);
  xnor xnor_23 (C24, in_1[24], in_2[24]);
  xnor xnor_24 (C25, in_1[25], in_2[25]);
  xnor xnor_25 (C14, in_1[14], in_2[14]);
  xnor xnor_26 (C15, in_1[15], in_2[15]);
  xnor xnor_27 (C26, in_1[26], in_2[26]);
  xnor xnor_28 (C27, in_1[27], in_2[27]);
  xnor xnor_29 (C28, in_1[28], in_2[28]);
  xnor xnor_30 (C29, in_1[29], in_2[29]);
  xnor xnor_31 (C30, in_1[30], in_2[30]);
  xnor xnor_32 (C31, in_1[31], in_2[31]);

  // Other names for the same wires on the sheet: A[31:0] = in_1; A0 = in_1[0]; A1 = in_1[1]; A2 = in_1[2];
  //   A3 = in_1[3]; A4 = in_1[4]; A5 = in_1[5]; A6 = in_1[6]; A7 = in_1[7]; A8 = in_1[8]; A9 = in_1[9];
  //   A10 = in_1[10]; A11 = in_1[11]; A12 = in_1[12]; A13 = in_1[13]; A14 = in_1[14]; A15 = in_1[15]; A16 = in_1[16];
  //   A17 = in_1[17]; A18 = in_1[18]; A19 = in_1[19]; A20 = in_1[20]; A21 = in_1[21]; A22 = in_1[22]; A23 = in_1[23];
  //   A24 = in_1[24]; A25 = in_1[25]; A26 = in_1[26]; A27 = in_1[27]; A28 = in_1[28]; A29 = in_1[29]; A30 = in_1[30];
  //   A31 = in_1[31]; B[31:0] = in_2; B0 = in_2[0]; B1 = in_2[1]; B2 = in_2[2]; B3 = in_2[3]; B4 = in_2[4];
  //   B5 = in_2[5]; B6 = in_2[6]; B7 = in_2[7]; B8 = in_2[8]; B9 = in_2[9]; B10 = in_2[10]; B11 = in_2[11];
  //   B12 = in_2[12]; B13 = in_2[13]; B14 = in_2[14]; B15 = in_2[15]; B16 = in_2[16]; B17 = in_2[17]; B18 = in_2[18];
  //   B19 = in_2[19]; B20 = in_2[20]; B21 = in_2[21]; B22 = in_2[22]; B23 = in_2[23]; B24 = in_2[24]; B25 = in_2[25];
  //   B26 = in_2[26]; B27 = in_2[27]; B28 = in_2[28]; B29 = in_2[29]; B30 = in_2[30]; B31 = in_2[31]
endmodule
