// Logisim project control_logic.circ as structural Verilog: 10 circuits, main circuit control_logic
module control_logic (
  input  [31:0] inst,
  input  BrEq,
  input  BrLt,
  output PCSel,
  output RegWEn,
  output [2:0] ImmSel,
  output BrUn,
  output out_8,
  output BSel,
  output [3:0] ALUSel,
  output MemRW,
  output [1:0] WBSel
);

  ASelSub aselsub_1 (.in_1(inst), .out_2(out_8));
  BSelSub bselsub_1 (.in_1(inst), .out_2(BSel));
  RegWEnSub regwensub_1 (.in_1(inst), .out_2(RegWEn));
  MemRWSub memrwsub_1 (.in_1(inst), .out_2(MemRW));
  ImmSelSub immselsub_1 (.in_1(inst), .out_2(ImmSel));
  BrUnSub brunsub_1 (.in_1(inst), .out_2(BrUn));
  WBSelSub wbselsub_1 (.in_1(inst), .out_2(WBSel));
  PCSelSub pcselsub_1 (.inst(inst), .BrEq(BrEq), .BrLt(BrLt), .out_4(PCSel));
  ALUSelSub aluselsub_1 (.in_1(inst), .out_2(ALUSel));

  // Other names for the same wires on the sheet: ASel = out_8

  // Notes on the sheet:
  //   INPUTS to your circuit
  //   DON'T CHANGE THE LOCATIONS OF THE INPUTS AND OUTPUTS!
  //   OUTPUT from your circuit
endmodule

module PCSelSub (
  input  [31:0] inst,
  input  BrEq,
  input  BrLt,
  output out_4
);

  wire b, beq, blt, f, f1, multiplexer_1_out, multiplexer_2_out, multiplexer_3_out, multiplexer_4_out,
       multiplexer_5_out, multiplexer_6_out, o, o1;
  wire [2:0] xnor_2_out, xnor_3_out;
  wire [6:0] xnor_1_out, xnor_4_out, xnor_5_out;

  assign xnor_1_out = ~(inst[6:0] ^ 7'b1100011);  // XNOR_Gate xnor_1, 7 bits wide
  assign xnor_2_out = ~(inst[14:12] ^ 3'b000);  // XNOR_Gate xnor_2, 3 bits wide
  assign xnor_3_out = ~(inst[14:12] ^ 3'b100);  // XNOR_Gate xnor_3, 3 bits wide
  assign xnor_4_out = ~(inst[6:0] ^ 7'b1100111);  // XNOR_Gate xnor_4, 7 bits wide
  assign xnor_5_out = ~(inst[6:0] ^ 7'b1101111);  // XNOR_Gate xnor_5, 7 bits wide
  Multiplexer #(.enable("false")) multiplexer_1 (.in0(1'b0), .in1(1'b1), .out(multiplexer_1_out), .sel(o1));
  Multiplexer #(.enable("false")) multiplexer_2 (.in0(1'b0), .in1(1'b1), .out(multiplexer_2_out), .sel(BrLt));
  Multiplexer #(.enable("false")) multiplexer_3 (.in0(1'b0), .in1(1'b1), .out(multiplexer_3_out), .sel(BrEq));
  Multiplexer #(.enable("false")) multiplexer_4 (.in0(multiplexer_1_out), .in1(1'b1), .out(multiplexer_4_out), .sel(o));
  Multiplexer #(.enable("false")) multiplexer_5 (
    .in0(1'b0), .in1(multiplexer_2_out), .out(multiplexer_5_out), .sel(blt));
  Multiplexer #(.enable("false")) multiplexer_6 (
    .in0(1'b0), .in1(multiplexer_3_out), .out(multiplexer_6_out), .sel(beq));
  and and_1 (b, xnor_1_out[0], xnor_1_out[1], xnor_1_out[2], xnor_1_out[3], xnor_1_out[4], xnor_1_out[5], xnor_1_out[6]);
  and and_2 (f, xnor_2_out[0], xnor_2_out[1], xnor_2_out[2]);
  and and_3 (f1, xnor_3_out[0], xnor_3_out[1], xnor_3_out[2]);
  and and_4 (o, xnor_4_out[0], xnor_4_out[1], xnor_4_out[2], xnor_4_out[3], xnor_4_out[4], xnor_4_out[5], xnor_4_out[6]);
  and and_5 (o1, xnor_5_out[0], xnor_5_out[1], xnor_5_out[2], xnor_5_out[3], xnor_5_out[4], xnor_5_out[5], xnor_5_out[6]);
  or or_1 (out_4, multiplexer_4_out, multiplexer_5_out, multiplexer_6_out);
  and and_6 (beq, b, f);
  and and_7 (blt, b, f1);
endmodule

module RegWEnSub (
  input  [31:0] in_1,
  output out_2
);

  wire multiplexer_1_out, multiplexer_2_out, multiplexer_3_out, multiplexer_4_out, o, o1, o2, o3, o4;
  wire [6:0] xnor_1_out, xnor_2_out, xnor_3_out, xnor_4_out, xnor_5_out;

  Multiplexer #(.enable("false")) multiplexer_1 (.in0(1'b0), .in1(1'b1), .out(multiplexer_1_out), .sel(o4));
  Multiplexer #(.enable("false")) multiplexer_2 (
    .in0(multiplexer_1_out), .in1(1'b1), .out(multiplexer_2_out), .sel(o3));
  assign xnor_1_out = ~(in_1[6:0] ^ 7'b1101111);  // XNOR_Gate xnor_1, 7 bits wide
  assign xnor_2_out = ~(in_1[6:0] ^ 7'b1100111);  // XNOR_Gate xnor_2, 7 bits wide
  assign xnor_3_out = ~(in_1[6:0] ^ 7'b0110011);  // XNOR_Gate xnor_3, 7 bits wide
  assign xnor_4_out = ~(in_1[6:0] ^ 7'b0010011);  // XNOR_Gate xnor_4, 7 bits wide
  assign xnor_5_out = ~(in_1[6:0] ^ 7'b0000011);  // XNOR_Gate xnor_5, 7 bits wide
  Multiplexer #(.enable("false")) multiplexer_3 (
    .in0(multiplexer_2_out), .in1(1'b1), .out(multiplexer_3_out), .sel(o2));
  Multiplexer #(.enable("false")) multiplexer_4 (
    .in0(multiplexer_3_out), .in1(1'b1), .out(multiplexer_4_out), .sel(o1));
  and and_1 (o, xnor_1_out[0], xnor_1_out[1], xnor_1_out[2], xnor_1_out[3], xnor_1_out[4], xnor_1_out[5], xnor_1_out[6]);
  and and_2 (o1, xnor_2_out[0], xnor_2_out[1], xnor_2_out[2], xnor_2_out[3], xnor_2_out[4], xnor_2_out[5], xnor_2_out[6]);
  and and_3 (o2, xnor_3_out[0], xnor_3_out[1], xnor_3_out[2], xnor_3_out[3], xnor_3_out[4], xnor_3_out[5], xnor_3_out[6]);
  and and_4 (o3, xnor_4_out[0], xnor_4_out[1], xnor_4_out[2], xnor_4_out[3], xnor_4_out[4], xnor_4_out[5], xnor_4_out[6]);
  and and_5 (o4, xnor_5_out[0], xnor_5_out[1], xnor_5_out[2], xnor_5_out[3], xnor_5_out[4], xnor_5_out[5], xnor_5_out[6]);
  Multiplexer #(.enable("false")) multiplexer_5 (.in0(multiplexer_4_out), .in1(1'b1), .out(out_2), .sel(o));

  // Other names for the same wires on the sheet: inst[31:0] = in_1
endmodule

module ImmSelSub (
  input  [31:0] in_1,
  output [2:0] out_2
);

  wire i, o, o1, o2, o3, o4, o5;
  wire [2:0] immsel, multiplexer_1_out, multiplexer_2_out, multiplexer_3_out;
  wire [6:0] xnor_1_out, xnor_2_out, xnor_3_out, xnor_4_out, xnor_5_out, xnor_6_out;

  Multiplexer #(.width(3), .enable("false")) multiplexer_1 (
    .in0(3'b000), .in1(3'b001), .out(multiplexer_1_out), .sel(i));
  Multiplexer #(.width(3), .enable("false")) multiplexer_2 (
    .in0(multiplexer_1_out), .in1(3'b010), .out(multiplexer_2_out), .sel(o3));
  Multiplexer #(.width(3), .enable("false")) multiplexer_3 (
    .in0(multiplexer_2_out), .in1(3'b011), .out(multiplexer_3_out), .sel(o4));
  assign xnor_1_out = ~(in_1[6:0] ^ 7'b0010011);  // XNOR_Gate xnor_1, 7 bits wide
  assign xnor_2_out = ~(in_1[6:0] ^ 7'b0000011);  // XNOR_Gate xnor_2, 7 bits wide
  assign xnor_3_out = ~(in_1[6:0] ^ 7'b1100111);  // XNOR_Gate xnor_3, 7 bits wide
  assign xnor_4_out = ~(in_1[6:0] ^ 7'b0100011);  // XNOR_Gate xnor_4, 7 bits wide
  assign xnor_5_out = ~(in_1[6:0] ^ 7'b1100011);  // XNOR_Gate xnor_5, 7 bits wide
  assign xnor_6_out = ~(in_1[6:0] ^ 7'b1101111);  // XNOR_Gate xnor_6, 7 bits wide
  Multiplexer #(.width(3), .enable("false")) multiplexer_4 (
    .in0(multiplexer_3_out), .in1(3'b101), .out(immsel), .sel(o5));
  and and_1 (o, xnor_1_out[0], xnor_1_out[1], xnor_1_out[2], xnor_1_out[3], xnor_1_out[4], xnor_1_out[5], xnor_1_out[6]);
  and and_2 (o1, xnor_2_out[0], xnor_2_out[1], xnor_2_out[2], xnor_2_out[3], xnor_2_out[4], xnor_2_out[5], xnor_2_out[6]);
  and and_3 (o2, xnor_3_out[0], xnor_3_out[1], xnor_3_out[2], xnor_3_out[3], xnor_3_out[4], xnor_3_out[5], xnor_3_out[6]);
  and and_4 (o3, xnor_4_out[0], xnor_4_out[1], xnor_4_out[2], xnor_4_out[3], xnor_4_out[4], xnor_4_out[5], xnor_4_out[6]);
  and and_5 (o4, xnor_5_out[0], xnor_5_out[1], xnor_5_out[2], xnor_5_out[3], xnor_5_out[4], xnor_5_out[5], xnor_5_out[6]);
  and and_6 (o5, xnor_6_out[0], xnor_6_out[1], xnor_6_out[2], xnor_6_out[3], xnor_6_out[4], xnor_6_out[5], xnor_6_out[6]);
  Multiplexer #(.select(3), .width(3), .enable("false")) multiplexer_5 (
    .in1(3'b001), .in2(3'b010), .in3(3'b011), .in5(3'b101), .out(out_2), .sel(immsel));  // open: in0, in4, in6, in7
  or or_1 (i, o, o1, o2);

  // Other names for the same wires on the sheet: inst[31:0] = in_1
endmodule

module BrUnSub (
  input  [31:0] in_1,
  output out_2
);

  wire o, o1, s;
  wire [2:0] xnor_2_out;
  wire [6:0] xnor_1_out;

  assign xnor_1_out = ~(in_1[6:0] ^ 7'b1100011);  // XNOR_Gate xnor_1, 7 bits wide
  assign xnor_2_out = ~(in_1[14:12] ^ 3'b100);  // XNOR_Gate xnor_2, 3 bits wide
  and and_1 (o, xnor_1_out[0], xnor_1_out[1], xnor_1_out[2], xnor_1_out[3], xnor_1_out[4], xnor_1_out[5], xnor_1_out[6]);
  Multiplexer #(.enable("false")) multiplexer_1 (.in0(1'b0), .in1(1'b0), .out(out_2), .sel(s));
  and and_2 (o1, xnor_2_out[0], xnor_2_out[1], xnor_2_out[2]);
  and and_3 (s, o, o1);

  // Other names for the same wires on the sheet: inst[31:0] = in_1
endmodule

module ASelSub (
  input  [31:0] in_1,
  output out_2
);

  wire multiplexer_1_out, multiplexer_2_out, multiplexer_3_out, multiplexer_4_out, o, o1, o2, o3, o4;
  wire [6:0] xnor_1_out, xnor_2_out, xnor_3_out, xnor_4_out, xnor_5_out;

  Multiplexer #(.enable("false")) multiplexer_1 (.in0(1'b0), .in1(1'b1), .out(multiplexer_1_out), .sel(o4));
  Multiplexer #(.enable("false")) multiplexer_2 (
    .in0(multiplexer_1_out), .in1(1'b1), .out(multiplexer_2_out), .sel(o3));
  assign xnor_1_out = ~(in_1[6:0] ^ 7'b0100011);  // XNOR_Gate xnor_1, 7 bits wide
  assign xnor_2_out = ~(in_1[6:0] ^ 7'b1100111);  // XNOR_Gate xnor_2, 7 bits wide
  assign xnor_3_out = ~(in_1[6:0] ^ 7'b0110011);  // XNOR_Gate xnor_3, 7 bits wide
  assign xnor_4_out = ~(in_1[6:0] ^ 7'b0010011);  // XNOR_Gate xnor_4, 7 bits wide
  assign xnor_5_out = ~(in_1[6:0] ^ 7'b0000011);  // XNOR_Gate xnor_5, 7 bits wide
  Multiplexer #(.enable("false")) multiplexer_3 (
    .in0(multiplexer_2_out), .in1(1'b1), .out(multiplexer_3_out), .sel(o2));
  Multiplexer #(.enable("false")) multiplexer_4 (
    .in0(multiplexer_3_out), .in1(1'b1), .out(multiplexer_4_out), .sel(o1));
  and and_1 (o, xnor_1_out[0], xnor_1_out[1], xnor_1_out[2], xnor_1_out[3], xnor_1_out[4], xnor_1_out[5], xnor_1_out[6]);
  and and_2 (o1, xnor_2_out[0], xnor_2_out[1], xnor_2_out[2], xnor_2_out[3], xnor_2_out[4], xnor_2_out[5], xnor_2_out[6]);
  and and_3 (o2, xnor_3_out[0], xnor_3_out[1], xnor_3_out[2], xnor_3_out[3], xnor_3_out[4], xnor_3_out[5], xnor_3_out[6]);
  and and_4 (o3, xnor_4_out[0], xnor_4_out[1], xnor_4_out[2], xnor_4_out[3], xnor_4_out[4], xnor_4_out[5], xnor_4_out[6]);
  and and_5 (o4, xnor_5_out[0], xnor_5_out[1], xnor_5_out[2], xnor_5_out[3], xnor_5_out[4], xnor_5_out[5], xnor_5_out[6]);
  Multiplexer #(.enable("false")) multiplexer_5 (.in0(multiplexer_4_out), .in1(1'b1), .out(out_2), .sel(o));

  // Other names for the same wires on the sheet: inst[31:0] = in_1
endmodule

module BSelSub (
  input  [31:0] in_1,
  output out_2
);

  wire o;
  wire [6:0] xnor_1_out;

  assign xnor_1_out = ~(in_1[6:0] ^ 7'b0110011);  // XNOR_Gate xnor_1, 7 bits wide
  Multiplexer #(.enable("false")) multiplexer_1 (.in0(1'b0), .in1(1'b1), .out(out_2), .sel(o));
  and and_1 (o, xnor_1_out[0], xnor_1_out[1], xnor_1_out[2], xnor_1_out[3], xnor_1_out[4], xnor_1_out[5], xnor_1_out[6]);

  // Other names for the same wires on the sheet: inst[31:0] = in_1
endmodule

module ALUSelSub (
  input  [31:0] in_1,
  output [3:0] out_2
);

  wire ADD, and_7_out, and_8_out, and_9_out, and_10_out, and_19_out, and_20_out, and_21_out, and_22_out,
       and_23_out, and_24_out, and_25_out, ANDD, f3_0, f3_1, f3_2, f3_4, f3_5, f3_6, f3_7, f7_0, f7_1, f7_20,
       MUL, MULH, o, ob, oi, ojal, ojalr, olw, ORR, osw, SLLL, SLT, SRAA, SUB, XORR;
  wire [2:0] xnor_8_out, xnor_9_out, xnor_10_out, xnor_11_out, xnor_12_out, xnor_13_out, xnor_14_out;
  wire [6:0] xnor_1_out, xnor_2_out, xnor_3_out, xnor_4_out, xnor_5_out, xnor_6_out, xnor_7_out, xnor_15_out,
       xnor_16_out, xnor_17_out;

  assign xnor_1_out = ~(in_1[6:0] ^ 7'b0110011);  // XNOR_Gate xnor_1, 7 bits wide
  assign xnor_2_out = ~(in_1[6:0] ^ 7'b0010011);  // XNOR_Gate xnor_2, 7 bits wide
  assign xnor_3_out = ~(in_1[6:0] ^ 7'b0000011);  // XNOR_Gate xnor_3, 7 bits wide
  assign xnor_4_out = ~(in_1[6:0] ^ 7'b0100011);  // XNOR_Gate xnor_4, 7 bits wide
  assign xnor_5_out = ~(in_1[6:0] ^ 7'b1100011);  // XNOR_Gate xnor_5, 7 bits wide
  assign xnor_6_out = ~(in_1[6:0] ^ 7'b1101111);  // XNOR_Gate xnor_6, 7 bits wide
  assign xnor_7_out = ~(in_1[6:0] ^ 7'b1100111);  // XNOR_Gate xnor_7, 7 bits wide
  and and_1 (SUB, o, f3_0, f7_20);
  and and_2 (MULH, o, f3_1, f7_1);
  and and_3 (MUL, o, f3_0, f7_1);
  and and_4 (SLT, o, f3_2, f7_0);
  and and_5 (SRAA, o, f3_5, f7_20);
  and and_6 (SLLL, o, f3_1, f7_0);
  and and_7 (and_7_out, o, f3_6, f7_0);
  and and_8 (and_8_out, oi, f3_6);
  and and_9 (and_9_out, o, f3_7, f7_0);
  and and_10 (and_10_out, oi, f3_7);
  and and_11 (XORR, oi, f3_4);
  or or_1 (ORR, and_7_out, and_8_out);
  or or_2 (ANDD, and_9_out, and_10_out);
  and and_12 (o, xnor_1_out[0], xnor_1_out[1], xnor_1_out[2], xnor_1_out[3], xnor_1_out[4], xnor_1_out[5], xnor_1_out[6]);
  and and_13 (oi, xnor_2_out[0], xnor_2_out[1], xnor_2_out[2], xnor_2_out[3], xnor_2_out[4], xnor_2_out[5], xnor_2_out[6]);
  and and_14 (olw, xnor_3_out[0], xnor_3_out[1], xnor_3_out[2], xnor_3_out[3], xnor_3_out[4], xnor_3_out[5], xnor_3_out[6]);
  and and_15 (osw, xnor_4_out[0], xnor_4_out[1], xnor_4_out[2], xnor_4_out[3], xnor_4_out[4], xnor_4_out[5], xnor_4_out[6]);
  and and_16 (ob, xnor_5_out[0], xnor_5_out[1], xnor_5_out[2], xnor_5_out[3], xnor_5_out[4], xnor_5_out[5], xnor_5_out[6]);
  and and_17 (ojal, xnor_6_out[0], xnor_6_out[1], xnor_6_out[2], xnor_6_out[3], xnor_6_out[4], xnor_6_out[5], xnor_6_out[6]);
  and and_18 (ojalr, xnor_7_out[0], xnor_7_out[1], xnor_7_out[2], xnor_7_out[3], xnor_7_out[4], xnor_7_out[5], xnor_7_out[6]);
  assign out_2 = SUB ? 4'b1000 : 4'bz;  // Controlled_Buffer controlled_buffer_1
  assign out_2 = SLT ? 4'b0111 : 4'bz;  // Controlled_Buffer controlled_buffer_2
  assign out_2 = SRAA ? 4'b0101 : 4'bz;  // Controlled_Buffer controlled_buffer_3
  assign out_2 = SLLL ? 4'b0110 : 4'bz;  // Controlled_Buffer controlled_buffer_4
  assign out_2 = ORR ? 4'b0010 : 4'bz;  // Controlled_Buffer controlled_buffer_5
  assign out_2 = XORR ? 4'b0011 : 4'bz;  // Controlled_Buffer controlled_buffer_6
  assign out_2 = ANDD ? 4'b0001 : 4'bz;  // Controlled_Buffer controlled_buffer_7
  assign xnor_8_out = ~(in_1[14:12] ^ 3'b000);  // XNOR_Gate xnor_8, 3 bits wide
  assign xnor_9_out = ~(in_1[14:12] ^ 3'b001);  // XNOR_Gate xnor_9, 3 bits wide
  assign xnor_10_out = ~(in_1[14:12] ^ 3'b010);  // XNOR_Gate xnor_10, 3 bits wide
  assign xnor_11_out = ~(in_1[14:12] ^ 3'b100);  // XNOR_Gate xnor_11, 3 bits wide
  assign xnor_12_out = ~(in_1[14:12] ^ 3'b101);  // XNOR_Gate xnor_12, 3 bits wide
  assign xnor_13_out = ~(in_1[14:12] ^ 3'b110);  // XNOR_Gate xnor_13, 3 bits wide
  assign xnor_14_out = ~(in_1[14:12] ^ 3'b111);  // XNOR_Gate xnor_14, 3 bits wide
  assign out_2 = MUL ? 4'b1001 : 4'bz;  // Controlled_Buffer controlled_buffer_8
  and and_19 (and_19_out, o, f3_0, f7_0);
  and and_20 (and_20_out, oi, f3_0);
  and and_21 (and_21_out, olw, f3_2);
  and and_22 (and_22_out, osw, f3_2);
  and and_23 (and_23_out, ob, f3_0);
  and and_24 (and_24_out, ob, f3_4);
  and and_25 (and_25_out, ojalr, f3_0);
  and and_26 (f3_0, xnor_8_out[0], xnor_8_out[1], xnor_8_out[2]);
  and and_27 (f3_1, xnor_9_out[0], xnor_9_out[1], xnor_9_out[2]);
  and and_28 (f3_2, xnor_10_out[0], xnor_10_out[1], xnor_10_out[2]);
  and and_29 (f3_4, xnor_11_out[0], xnor_11_out[1], xnor_11_out[2]);
  and and_30 (f3_5, xnor_12_out[0], xnor_12_out[1], xnor_12_out[2]);
  and and_31 (f3_6, xnor_13_out[0], xnor_13_out[1], xnor_13_out[2]);
  and and_32 (f3_7, xnor_14_out[0], xnor_14_out[1], xnor_14_out[2]);
  or or_3 (ADD, and_19_out, and_20_out, and_21_out, and_22_out, and_23_out, and_24_out, and_25_out, ojal);
  assign out_2 = ADD ? 4'b0000 : 4'bz;  // Controlled_Buffer controlled_buffer_9
  assign xnor_15_out = ~(in_1[31:25] ^ {7{1'b0}});  // XNOR_Gate xnor_15, 7 bits wide
  assign xnor_16_out = ~(in_1[31:25] ^ 7'b0000001);  // XNOR_Gate xnor_16, 7 bits wide
  assign xnor_17_out = ~(in_1[31:25] ^ 7'b0100000);  // XNOR_Gate xnor_17, 7 bits wide
  and and_33 (f7_0, xnor_15_out[0], xnor_15_out[1], xnor_15_out[2], xnor_15_out[3], xnor_15_out[4], xnor_15_out[5], xnor_15_out[6]);
  and and_34 (f7_1, xnor_16_out[0], xnor_16_out[1], xnor_16_out[2], xnor_16_out[3], xnor_16_out[4], xnor_16_out[5], xnor_16_out[6]);
  and and_35 (f7_20, xnor_17_out[0], xnor_17_out[1], xnor_17_out[2], xnor_17_out[3], xnor_17_out[4], xnor_17_out[5], xnor_17_out[6]);

  // Other names for the same wires on the sheet: ALUSelect[3:0] = out_2; inst[31:0] = in_1
endmodule

module MemRWSub (
  input  [31:0] in_1,
  output out_2
);

  wire o;
  wire [6:0] xnor_1_out;

  assign xnor_1_out = ~(in_1[6:0] ^ 7'b0100011);  // XNOR_Gate xnor_1, 7 bits wide
  Multiplexer #(.enable("false")) multiplexer_1 (.in0(1'b0), .in1(1'b1), .out(out_2), .sel(o));
  and and_1 (o, xnor_1_out[0], xnor_1_out[1], xnor_1_out[2], xnor_1_out[3], xnor_1_out[4], xnor_1_out[5], xnor_1_out[6]);

  // Other names for the same wires on the sheet: inst[31:0] = in_1
endmodule

module WBSelSub (
  input  [31:0] in_1,
  output [1:0] out_2
);

  wire alu, o, o1, o2, o3, o4, pc;
  wire [1:0] multiplexer_1_out, multiplexer_2_out, wb;
  wire [6:0] xnor_1_out, xnor_2_out, xnor_3_out, xnor_4_out, xnor_5_out;

  Multiplexer #(.width(2), .enable("false")) multiplexer_1 (
    .in0(2'b00), .in1(2'b01), .out(multiplexer_1_out), .sel(alu));
  Multiplexer #(.width(2), .enable("false")) multiplexer_2 (
    .in0(multiplexer_1_out), .in1(2'b10), .out(multiplexer_2_out), .sel(o2));
  Multiplexer #(.width(2), .enable("false")) multiplexer_3 (.in0(multiplexer_2_out), .in1(2'b11), .out(wb), .sel(pc));
  assign xnor_1_out = ~(in_1[6:0] ^ 7'b0110011);  // XNOR_Gate xnor_1, 7 bits wide
  assign xnor_2_out = ~(in_1[6:0] ^ 7'b0010011);  // XNOR_Gate xnor_2, 7 bits wide
  assign xnor_3_out = ~(in_1[6:0] ^ 7'b0000011);  // XNOR_Gate xnor_3, 7 bits wide
  assign xnor_4_out = ~(in_1[6:0] ^ 7'b1100111);  // XNOR_Gate xnor_4, 7 bits wide
  assign xnor_5_out = ~(in_1[6:0] ^ 7'b1101111);  // XNOR_Gate xnor_5, 7 bits wide
  and and_1 (o, xnor_1_out[0], xnor_1_out[1], xnor_1_out[2], xnor_1_out[3], xnor_1_out[4], xnor_1_out[5], xnor_1_out[6]);
  and and_2 (o1, xnor_2_out[0], xnor_2_out[1], xnor_2_out[2], xnor_2_out[3], xnor_2_out[4], xnor_2_out[5], xnor_2_out[6]);
  and and_3 (o2, xnor_3_out[0], xnor_3_out[1], xnor_3_out[2], xnor_3_out[3], xnor_3_out[4], xnor_3_out[5], xnor_3_out[6]);
  and and_4 (o3, xnor_4_out[0], xnor_4_out[1], xnor_4_out[2], xnor_4_out[3], xnor_4_out[4], xnor_4_out[5], xnor_4_out[6]);
  and and_5 (o4, xnor_5_out[0], xnor_5_out[1], xnor_5_out[2], xnor_5_out[3], xnor_5_out[4], xnor_5_out[5], xnor_5_out[6]);
  Multiplexer #(.select(2), .width(2), .enable("false")) multiplexer_4 (
    .in1(2'b01), .in2(2'b10), .in3(2'b11), .out(out_2), .sel(wb));  // open: in0
  or or_1 (alu, o, o1);
  or or_2 (pc, o3, o4);

  // Other names for the same wires on the sheet: inst[31:0] = in_1
endmodule
