// Logisim project cpu.circ as structural Verilog: 1 circuit, main circuit main
module main (
  input  [31:0] INSTRUCTION,
  input  CLOCK,
  output [31:0] PROGRAM_COUNTER,
  output [31:0] ra,
  output [31:0] sp,
  output [31:0] t0,
  output [31:0] t1,
  output [31:0] t2,
  output [31:0] s0,
  output [31:0] s1,
  output [31:0] a0
);

  wire ASel, BrEq, BrLt, BrUn, BSel, jump, MemRW, PCSel, RegWEn;
  wire [1:0] WBSel;
  wire [2:0] funct3, ImmSel;
  wire [3:0] ALUSel;
  wire [6:0] funct7;
  wire [24:0] jINSTRUCTION;
  wire [31:0] A, ALUR, B, dataA, dataB, imm, INSTRUCTION2, multiplexer_1_out, PC, PC4, PC_4, rdata, wb;

  control_logic control_logic_1 (
    .BSel(BSel), .BrUn(BrUn), .RegWEn(RegWEn), .ImmSel(ImmSel), .out_8(ASel), .PCSel(PCSel), .BrLt(BrLt),
    .BrEq(BrEq), .inst({funct7, jINSTRUCTION[24:15], funct3, jINSTRUCTION[11:0]}), .ALUSel(ALUSel),
    .MemRW(MemRW), .WBSel(WBSel));
  Multiplexer #(.width(32), .enable("false")) multiplexer_1 (
    .in0(PC4), .in1(ALUR), .out(multiplexer_1_out), .sel(PCSel));
  D_Flip_Flop #(.trigger("falling")) d_ff_1 (.D(PCSel), .clk(CLOCK), .Q(jump));  // open: Qn, preset, reset
  fallingsadness fallingsadness_1 (.clk(CLOCK), .WE(1'b1), .in_4(INSTRUCTION), .out_5(INSTRUCTION2));  // open: reset
  Multiplexer #(.width(32), .enable("false")) multiplexer_2 (
    .in0(INSTRUCTION2), .in1(32'h13), .out({funct7, jINSTRUCTION[24:15], funct3, jINSTRUCTION[11:0]}),
    .sel(PCSel));
  add32 add32_1 (.in_1(PROGRAM_COUNTER), .in_2(32'h4), .Cin(1'b0), .out_4(PC4));  // open: Cout
  fallingsadness fallingsadness_2 (
    .clk(CLOCK), .WE(1'b1), .in_4(multiplexer_1_out), .out_5(PROGRAM_COUNTER));  // open: reset
  fallingsadness fallingsadness_3 (.clk(CLOCK), .WE(1'b1), .in_4(PROGRAM_COUNTER), .out_5(PC));  // open: reset
  imm_gen imm_gen_1 (.ImmSel(ImmSel), .imm(imm), .inst({funct7, jINSTRUCTION[24:15], funct3, jINSTRUCTION[11:0]}));
  regfile_main RegFile (
    .rs2(jINSTRUCTION[24:20]), .rd(jINSTRUCTION[11:7]), .Read_Data_1(dataA), .Read_Data_2(dataB), .ra(ra),
    .sp(sp), .t0(t0), .t1(t1), .t2(t2), .s0(s0), .s1(s1), .a0(a0), .rs1(jINSTRUCTION[19:15]),
    .Write_Data(wb), .RegWEn(RegWEn), .clk(CLOCK));
  branch_comp branch_comp_1 (.BrEq(BrEq), .rs1(dataA), .rs2(dataB), .BrLt(BrLt), .BrUn(BrUn));
  Multiplexer #(.width(32), .enable("false")) multiplexer_3 (.in0(imm), .in1(dataB), .out(B), .sel(BSel));
  Multiplexer #(.width(32), .enable("false")) multiplexer_4 (.in0(PC), .in1(dataA), .out(A), .sel(ASel));
  alu Arithmetic_Logic_Unit (.Result(ALUR), .ALUSel(ALUSel), .A(A), .B(B));
  // mem_main DMEM: pin names not known; wires that end beside it: ALUR, dataB, CLOCK, MemRW, rdata
  add32 add32_2 (.in_1(PC), .in_2(32'h4), .Cin(1'b0), .out_4(PC_4));  // open: Cout
  Multiplexer #(.select(2), .width(32), .enable("false")) multiplexer_5 (
    .in1(ALUR), .in2(rdata), .in3(PC_4), .out(wb), .sel(WBSel));  // open: in0

  // Other names for the same wires on the sheet: clk = CLOCK; opcode[6:0] = jINSTRUCTION[6:0];
  //   rd[4:0] = jINSTRUCTION[11:7]; jINSTRUCTION (some bits) = {funct7, funct3}; rs1[4:0] = jINSTRUCTION[19:15];
  //   rs2[4:0] = jINSTRUCTION[24:20]

  // Notes on the sheet:
  //   Output
  //   IMEM (do **NOT** move this)
  //   Inputs
  //   It is OK to move the PC, RegFile, ALU, MEM, Branch Comp, Imm Gen, and Control Logic to wherever is most convenient for you when constructing your CPU, and to delete this text
  //   Inputs/Outputs for testing. Do **NOT** move these.
endmodule
